# Fritzing sketch MarioTouch (saved by Fritzing 0.7.10b)
breadboards: 1

parts:
  J1 = Piezo Speaker
  U1 = DS_TOUCH_CONNECTOR [package=ds_touch_connector]
  R1 = Resistor [tolerance=±5% resistance=10k package=THT]
  R2 = Resistor [tolerance=±5% resistance=10k package=THT]
  R3 = Resistor [tolerance=±5% resistance=10k package=THT]
  R4 = Resistor [tolerance=±5% resistance=10k package=THT]
  Arduino2 = Arduino Fio

nets:
  N1: J1.pin1, R1.Pin_0, R2.Pin_0, R3.Pin_0, R4.Pin_0, Arduino2.GND
  N2: U1.X1, R1.Pin_1, Arduino2.A0
  N3: U1.Y2, R4.Pin_1, Arduino2.A3
  N4: U1.X2, R2.Pin_1, Arduino2.A1
  N5: U1.Y1, R3.Pin_1, Arduino2.A2
